# Fritzing sketch Aaron_Circuit (saved by Fritzing 1.0.0rc)
breadboards: 1

parts:
  Q1 = NPN-Transistor [package="TO92 [THT]"]
  R1 = Resistor [tolerance=±5% power=0.25W resistance=220 package=THT]
  R2 = Resistor [tolerance=±5% power=0.25W resistance=220 package=THT]
  J1 = Basic Servo
  Part1 = Arduino Uno (Rev3)
  Part2 = 16-Channel 12-bit PWM Servo Driver - I2C [part_number=815]
  Power_plug1 = Power plug
  U1 = RELAY [package=relay-g5q]
  F1 = Resettable Fuse PTC [package=ptc]
  J2 = Basic Servo
  F2 = Resettable Fuse PTC [package=ptc]
  J3 = Basic Servo
  F3 = Resettable Fuse PTC [package=ptc]
  J4 = Basic Servo
  F4 = Resettable Fuse PTC [package=ptc]
  J5 = Basic Servo
  F5 = Resettable Fuse PTC [package=ptc]
  J6 = Basic Servo
  F6 = Resettable Fuse PTC [package=ptc]
  J7 = Basic Servo
  F7 = Resettable Fuse PTC [package=ptc]
  J8 = Basic Servo
  F8 = Resettable Fuse PTC [package=ptc]
  J9 = Basic Servo
  F9 = Resettable Fuse PTC [package=ptc]
  J10 = Basic Servo
  F10 = Resettable Fuse PTC [package=ptc]
  J11 = Basic Servo
  F11 = Resettable Fuse PTC [package=ptc]
  J12 = Basic Servo
  F12 = Resettable Fuse PTC [package=ptc]
  J13 = Basic Servo
  F13 = Resettable Fuse PTC [package=ptc]
  J14 = Basic Servo
  F14 = Resettable Fuse PTC [package=ptc]
  J15 = Basic Servo
  F15 = Resettable Fuse PTC [package=ptc]
  J16 = Basic Servo
  F16 = Resettable Fuse PTC [package=ptc]
  J17 = Basic Servo
  F17 = Resettable Fuse PTC [package=ptc]
  J18 = Basic Servo
  F18 = Resettable Fuse PTC [package=ptc]
  J19 = Basic Servo
  F19 = Resettable Fuse PTC [package=ptc]
  J20 = Basic Servo
  F20 = Resettable Fuse PTC [package=ptc]
  J21 = Basic Servo
  F21 = Resettable Fuse PTC [package=ptc]
  Part3 = NeoPixel NeoMatrix 8x8 [part_number=1487]
  Part4 = NeoPixel NeoMatrix 8x8 [part_number=1487]

nets:
  GND: Q1.E, R1.Pin_0, J1.gnd, Part1.GND, Part2.GND, Power_plug1.GND, J2.gnd, J3.gnd, J4.gnd, J5.gnd, J6.gnd, J7.gnd, J8.gnd, J9.gnd, J10.gnd, J11.gnd, J12.gnd, J13.gnd, J14.gnd, J15.gnd, J16.gnd, J17.gnd, J18.gnd, J19.gnd, J20.gnd, J21.gnd, Part3.GND, Part4.GND
  N1: Q1.B, R1.Pin_1, R2.Pin_0
  N2: Q1.C, U1.COIL2
  N3: R2.Pin_1, Part1.D2
  N4: J1.vcc, F1.2
  N5: J1.pulse, Part2.PWM0
  N6: Part1.A4/SDA, Part2.SDA
  N7: Part1.A5/SCL, Part2.SCL
  N8: Part1.D4, Part3.IN
  N9: Part1.D7, Part4.IN
  5V: Part1.5V, Part2.VCC, U1.COIL1
  N10: Part2.PWM7, J8.pulse
  N11: Part2.PWM6, J7.pulse
  N12: Part2.PWM5, J6.pulse
  N13: Part2.PWM4, J5.pulse
  N14: Part2.PWM3, J4.pulse
  N15: Part2.PWM2, J3.pulse
  N16: Part2.PWM1, J2.pulse
  N17: Part2.PWM15, J16.pulse
  N18: Part2.PWM14, J15.pulse
  N19: Part2.PWM13, J14.pulse
  N20: Part2.PWM12, J13.pulse
  N21: Part2.PWM11, J12.pulse
  N22: Part2.PWM10, J11.pulse
  N23: Part2.PWM9, J10.pulse
  N24: Part2.PWM8, J9.pulse
  VDD: Power_plug1.VCC, U1.MAIN, Part3.VDD, Part4.VDD
  N25: J2.vcc, F2.2
  N26: J3.vcc, F3.2
  N27: J4.vcc, F4.2
  N28: J5.vcc, F5.2
  N29: J6.vcc, F6.2
  N30: J7.vcc, F7.2
  N31: J8.vcc, F8.2
  N32: J9.vcc, F9.2
  N33: J10.vcc, F10.2
  N34: J11.vcc, F11.2
  N35: J12.vcc, F12.2
  N36: J13.vcc, F13.2
  N37: J14.vcc, F14.2
  N38: J15.vcc, F15.2
  N39: J16.vcc, F16.2
  N40: J17.vcc, F17.2
  N41: J18.vcc, F18.2
  N42: J19.vcc, F19.2
  N43: J20.vcc, F20.2
  N44: J21.vcc, F21.2

custom parts:
  16-Channel 12-bit PWM Servo Driver - I2C: You want to make a cool robot, maybe a hexapod walker, or maybe just a piece of art with a lot of moving parts. Or maybe you want to drive a lot of LEDs with precise PWM output. Using only two pins, control 16 free-running PWM outputs! You can even chain up 62 breakouts to control up to 992 PWM outputs.
  NeoPixel NeoMatrix 8x8: Put on your sunglasses before wiring up this LED matrix - 64 eye-blistering RGB LEDs adorn the NeoMatrix for a blast of configurable color. Arranged in an 8x8 matrix, each pixel is individually addressable. Only one microcontroller pin is required to control all the LEDs, and you get 24 bit color for each LED.
